// Logisim project H1.circ as structural Verilog: 10 circuits, main circuit P1
module P1 (
  input  I2,
  input  I1,
  input  I0,
  output A,
  output B,
  output C,
  output D,
  output E,
  output F,
  output G,
  output H
);

  and u_A (A, ~I0, ~I1, ~I2);  // AND_Gate
  and u_B (B, I0, ~I1, ~I2);  // AND_Gate
  and u_C (C, ~I0, I1, ~I2);  // AND_Gate
  and u_D (D, I0, I1, ~I2);  // AND_Gate
  and u_E (E, ~I0, ~I1, I2);  // AND_Gate
  and u_F (F, I0, ~I1, I2);  // AND_Gate
  and u_G (G, ~I0, I1, I2);  // AND_Gate
  and u_H (H, I0, I1, I2);

  // Notes on the sheet:
  //   PROBLEM 1: DECODER
  //   INPUT SECTION: Do not change anything here!
  //   You may only change the values of the inputs for testing using the hand tool.
  //   Do not introduce any other input or output pins.
  //   To your logic
  //   OUTPUT SECTION: Do not change anything here!
  //   Do not introduce any other input or output pins.
  //   From your logic
endmodule

module P2 (
  input  A,
  input  B,
  input  C,
  output X,
  output Y
);

  wire A_out, D_out, F_out, G_out, H_out;

  and u_A (A_out, ~C, ~B, ~A);  // AND_Gate
  // AND_Gate B has open pins: in0=C, in1=B, in2=A, out=open
  // AND_Gate C has open pins: in0=C, in1=B, in2=A, out=open
  and D (D_out, C, B, ~A);  // AND_Gate
  // AND_Gate E has open pins: in0=C, in1=B, in2=A, out=open
  and F (F_out, C, ~B, A);  // AND_Gate
  and G (G_out, ~C, B, A);  // AND_Gate
  and H (H_out, C, B, A);
  or or_1 (X, A_out, D_out, F_out, G_out);
  or or_2 (Y, A_out, H_out);

  // Notes on the sheet:
  //   PROBLEM 2: PROGRAMMABLE LOGIC ARRAY
  //   INPUT SECTION: Do not change anything here!
  //   You may only change the values of the inputs for testing using the hand tool.
  //   Do not introduce any other input or output pins.
  //   To your logic
  //   OUTPUT SECTION: Do not change anything here!
  //   Do not introduce any other input or output pins.
  //   From your logic
endmodule

module P3 (
  input  A,
  input  B,
  input  C,
  output X
);

  wire transistor_1_out, transistor_2_out, transistor_7_out, transistor_8_out;

  Transistor transistor_1 (.in(transistor_2_out), .out(transistor_1_out), .gate(A));
  Transistor transistor_2 (.in(1'b1), .out(transistor_2_out), .gate(A));
  Transistor transistor_3 (.in(1'b1), .out(transistor_2_out), .gate(C));
  Transistor transistor_4 (.in(transistor_2_out), .out(transistor_1_out), .gate(B));
  Transistor transistor_5 (.in(transistor_1_out), .out(X), .gate(C));
  Transistor transistor_6 (.in(transistor_2_out), .out(transistor_1_out), .gate(C));
  Transistor transistor_7 (.in(1'b1), .out(transistor_7_out), .gate(A));
  Transistor transistor_8 (.in(transistor_7_out), .out(transistor_8_out), .gate(C));
  Transistor transistor_9 (.in(transistor_7_out), .out(X), .gate(B));
  Transistor transistor_10 (.in(transistor_8_out), .out(X), .gate(A));

  // Other names for the same wires on the sheet: tA = A; tB = B; tC = C

  // Notes on the sheet:
  //   PROBLEM 3: SERIES-PARALLEL CIRCUITS OF TRANSISTORS
  //   RESERVED SECTION: Do not change anything here!
  //   You may only change the values of the inputs for testing using the hand tool.
  //   Do not introduce any other input or output pins.
  //   From your pull-down circuit
endmodule

module P4_Main (
  input  A11,
  input  A10,
  input  A9,
  input  A8,
  input  A7,
  input  A6,
  input  A5,
  input  A4,
  input  A3,
  input  A2,
  input  A1,
  input  A0,
  output X11,
  output X10,
  output X9,
  output X8,
  output X7,
  output X6,
  output X5,
  output X4,
  output X3,
  output X2,
  output X1,
  output X0
);

  wire p4_incrbit0_1_cout, p4_incronebit_1_cout, p4_incronebit_2_cout, p4_incronebit_3_cout,
       p4_incronebit_4_cout, p4_incronebit_5_cout, p4_incronebit_6_cout, p4_incronebit_7_cout,
       p4_incronebit_8_cout, p4_incronebit_9_cout, p4_incronebit_10_cout;

  P4_IncrBit0 p4_incrbit0_1 (.A(A0), .S(X0), .Cout(p4_incrbit0_1_cout));
  P4_IncrOneBit p4_incronebit_1 (.Cin(p4_incrbit0_1_cout), .A(A1), .S(X1), .Cout(p4_incronebit_1_cout));
  P4_IncrOneBit p4_incronebit_2 (.Cin(p4_incronebit_1_cout), .A(A2), .S(X2), .Cout(p4_incronebit_2_cout));
  P4_IncrOneBit p4_incronebit_3 (.Cin(p4_incronebit_2_cout), .A(A3), .S(X3), .Cout(p4_incronebit_3_cout));
  P4_IncrOneBit p4_incronebit_4 (.Cin(p4_incronebit_3_cout), .A(A4), .S(X4), .Cout(p4_incronebit_4_cout));
  P4_IncrOneBit p4_incronebit_5 (.Cin(p4_incronebit_4_cout), .A(A5), .S(X5), .Cout(p4_incronebit_5_cout));
  P4_IncrOneBit p4_incronebit_6 (.Cin(p4_incronebit_5_cout), .A(A6), .S(X6), .Cout(p4_incronebit_6_cout));
  P4_IncrOneBit p4_incronebit_7 (.Cin(p4_incronebit_6_cout), .A(A7), .S(X7), .Cout(p4_incronebit_7_cout));
  P4_IncrOneBit p4_incronebit_8 (.Cin(p4_incronebit_7_cout), .A(A8), .S(X8), .Cout(p4_incronebit_8_cout));
  P4_IncrOneBit p4_incronebit_9 (.Cin(p4_incronebit_8_cout), .A(A9), .S(X9), .Cout(p4_incronebit_9_cout));
  P4_IncrOneBit p4_incronebit_10 (.Cin(p4_incronebit_9_cout), .A(A10), .S(X10), .Cout(p4_incronebit_10_cout));
  P4_IncrOneBit p4_incronebit_11 (.Cin(p4_incronebit_10_cout), .A(A11), .S(X11));  // open: Cout

  // Notes on the sheet:
  //   PROBLEM 4: 12-BIT INCREMENTER (Main)
  //   INPUT SECTION: Do not change anything here!
  //   You may only change the values of the inputs for testing using the hand tool.
  //   Do not introduce any other input or output pins.
  //   To your logic
  //   OUTPUT SECTION: Do not change anything here!
  //   Do not introduce any other input or output pins.
  //   From your logic
endmodule

module P4_IncrOneBit (
  input  Cin,
  input  A,
  output S,
  output Cout
);

  xor xor_1 (S, Cin, A);
  and and_1 (Cout, Cin, A);

  // Notes on the sheet:
  //   PROBLEM 4: 12-BIT INCREMENTER (IncrOneBit)
  //   INPUT SECTION: Do not change anything here!
  //   You may only change the values of the inputs for testing using the hand tool.
  //   Do not introduce any other input or output pins.
  //   To your logic
  //   OUTPUT SECTION: Do not change anything here!
  //   Do not introduce any other input or output pins.
  //   From your logic
endmodule

module P4_IncrBit0 (
  input  A,
  output S,
  output Cout
);

  not not_1 (S, A);

  assign Cout = A;

  // Notes on the sheet:
  //   PROBLEM 4: 12-BIT INCREMENTER (IncrBit0)
  //   INPUT SECTION: Do not change anything here!
  //   You may only change the values of the inputs for testing using the hand tool.
  //   Do not introduce any other input or output pins.
  //   To your logic
  //   OUTPUT SECTION: Do not change anything here!
  //   Do not introduce any other input or output pins.
  //   From your logic
endmodule

module P5_Main (
  input  A10,
  input  A9,
  input  A8,
  input  A7,
  input  A6,
  input  A5,
  input  A4,
  input  A3,
  input  A2,
  input  A1,
  input  A0,
  output X10,
  output X9,
  output X8,
  output X7,
  output X6,
  output X5,
  output X4,
  output X3,
  output X2,
  output X1,
  output X0
);

  wire [10:0] p5_clsh1_1_y, p5_clsh1_2_y, p5_clsh1_3_y, p5_clsh1_4_y, p5_clsh1_5_y, p5_clsh1_6_y,
       p5_clsh1_7_y, p5_clsh1_8_y, p5_clsh1_9_y, p5_clsh1_10_y;

  P5_CLSH1 p5_clsh1_1 (.X({A10, A9, A8, A7, A6, A5, A4, A3, A2, A1, A0}), .Y(p5_clsh1_1_y));
  P5_CLSH1 p5_clsh1_2 (.X(p5_clsh1_1_y), .Y(p5_clsh1_2_y));
  P5_CLSH1 p5_clsh1_3 (.X(p5_clsh1_2_y), .Y(p5_clsh1_3_y));
  P5_CLSH1 p5_clsh1_4 (.X(p5_clsh1_3_y), .Y(p5_clsh1_4_y));
  P5_CLSH1 p5_clsh1_5 (.X(p5_clsh1_4_y), .Y(p5_clsh1_5_y));
  P5_CLSH1 p5_clsh1_6 (.X(p5_clsh1_5_y), .Y(p5_clsh1_6_y));
  P5_CLSH1 p5_clsh1_7 (.X(p5_clsh1_6_y), .Y(p5_clsh1_7_y));
  P5_CLSH1 p5_clsh1_8 (.X(p5_clsh1_7_y), .Y(p5_clsh1_8_y));
  P5_CLSH1 p5_clsh1_9 (.X(p5_clsh1_8_y), .Y(p5_clsh1_9_y));
  P5_CLSH1 p5_clsh1_10 (.X(p5_clsh1_9_y), .Y(p5_clsh1_10_y));
  P5_CLSH1 p5_clsh1_11 (.X(p5_clsh1_10_y), .Y({X10, X9, X8, X7, X6, X5, X4, X3, X2, X1, X0}));

  // Notes on the sheet:
  //   PROBLEM 5: 11-BIT LEFT NORMALIZER (Main)
  //   INPUT SECTION: Do not change anything here!
  //   You may only change the values of the inputs for testing using the hand tool.
  //   Do not introduce any other input or output pins.
  //   To your logic
  //   OUTPUT SECTION: Do not change anything here!
  //   Do not introduce any other input or output pins.
  //   From your logic
endmodule

module P5_LSH1 (
  input  [10:0] X,
  output [10:0] Y
);


  assign Y = {X[9:0], 1'b0};

  // Notes on the sheet:
  //   PROBLEM 5: 11-BIT LEFT NORMALIZER (LSH1)
  //   INPUT SECTION: Do not change anything here!
  //   You may only change the values of the inputs for testing using the hand tool.
  //   Do not introduce any other input or output pins.
  //   To your logic
  //   OUTPUT SECTION: Do not change anything here!
  //   Do not introduce any other input or output pins.
  //   From your logic
endmodule

module P5_Mux11 (
  input  S,
  input  [10:0] A,
  input  [10:0] B,
  output [10:0] X
);

  wire [10:0] and_1_out, and_2_out, not_1_out;

  assign not_1_out = ~{11{S}};  // NOT_Gate not_1, 11 bits wide
  assign and_1_out = A & not_1_out;  // AND_Gate and_1, 11 bits wide
  assign and_2_out = B & {11{S}};  // AND_Gate and_2, 11 bits wide
  assign X = and_1_out | and_2_out;  // OR_Gate or_1, 11 bits wide

  // Notes on the sheet:
  //   PROBLEM 5: 11-BIT LEFT NORMALIZER (Mux11)
  //   INPUT SECTION: Do not change anything here!
  //   You may only change the values of the inputs for testing using the hand tool.
  //   Do not introduce any other input or output pins.
  //   To your logic
  //   OUTPUT SECTION: Do not change anything here!
  //   Do not introduce any other input or output pins.
  //   From your logic
endmodule

module P5_CLSH1 (
  input  [10:0] X,
  output [10:0] Y
);

  wire [10:0] p5_lsh1_1_y;

  P5_LSH1 p5_lsh1_1 (.X(X), .Y(p5_lsh1_1_y));
  P5_Mux11 p5_mux11_1 (.S(X[10]), .A(p5_lsh1_1_y), .B(X), .X(Y));

  // Notes on the sheet:
  //   PROBLEM 5: 11-BIT LEFT NORMALIZER (CLSH1)
  //   INPUT SECTION: Do not change anything here!
  //   You may only change the values of the inputs for testing using the hand tool.
  //   Do not introduce any other input or output pins.
  //   To your logic
  //   OUTPUT SECTION: Do not change anything here!
  //   Do not introduce any other input or output pins.
  //   From your logic
endmodule
