// Logisim project H2.circ as structural Verilog: 2 circuits, main circuit P2
module P2 (
  input  S1,
  input  S0,
  input  In,
  output S1n,
  output S0n,
  output Out
);

  wire and_1_out, and_2_out, and_3_out, and_4_out, and_5_out, and_7_out, and_8_out;

  and and_1 (and_1_out, ~In, ~S0, ~S1);  // AND_Gate
  and and_2 (and_2_out, In, ~S0, ~S1);  // AND_Gate
  and and_3 (and_3_out, ~In, S0, ~S1);  // AND_Gate
  and and_4 (and_4_out, In, S0, ~S1);  // AND_Gate
  and and_5 (and_5_out, ~In, ~S0, S1);  // AND_Gate
  // AND_Gate and_6 has open pins: in0=In, in1=S0, in2=S1, out=open
  and and_7 (and_7_out, ~In, S0, S1);  // AND_Gate
  and and_8 (and_8_out, In, S0, S1);
  or or_1 (S1n, and_1_out, and_5_out, and_7_out);
  or or_2 (S0n, and_2_out, and_4_out, and_5_out);
  or or_3 (Out, and_2_out, and_3_out, and_5_out, and_7_out, and_8_out);

  // Notes on the sheet:
  //   PROBLEM 2: IMPLEMENTING A STATE TABLE
  //   INPUT SECTION: Do not change anything here!
  //   You may only change the values of the inputs for testing using the hand tool.
  //   Do not introduce any other input or output pins in the circuit.
  //   To your logic
  //   OUTPUT SECTION: Do not change anything here!
  //   Do not introduce any other input or output pins in the circuit.
  //   From your logic
endmodule

module P3 (
  input  In,
  output Out
);

  wire and_1_out, and_3_out, and_4_out, and_5_out, and_7_out, and_8_out, and_9_out, and_11_out, and_12_out,
       and_14_out, clock_1_out, S0, S0_q, S1, S1_q, S2, S2_q;

  D_Flip_Flop u_S2 (.clk(clock_1_out), .D(S2), .Q(S2_q));  // open: Qn, preset, en, reset
  Clock clock_1 (.out(clock_1_out));
  D_Flip_Flop u_S1 (.clk(clock_1_out), .D(S1), .Q(S1_q));  // open: Qn, preset, en, reset
  D_Flip_Flop u_S0 (.clk(clock_1_out), .D(S0), .Q(S0_q));  // open: Qn, preset, en, reset
  and and_1 (and_1_out, ~S2_q, ~S1_q, ~S0_q, ~In);  // AND_Gate
  // AND_Gate and_2 has open pins: in0=S2_q, in1=S1_q, in2=S0_q, in3=In, out=open
  and and_3 (and_3_out, ~S2_q, ~S1_q, S0_q, ~In);  // AND_Gate
  and and_4 (and_4_out, ~S2_q, ~S1_q, S0_q, In);  // AND_Gate
  and and_5 (and_5_out, ~S2_q, S1_q, ~S0_q, ~In);  // AND_Gate
  // AND_Gate and_6 has open pins: in0=S2_q, in1=S1_q, in2=S0_q, in3=In, out=open
  and and_7 (and_7_out, ~S2_q, S1_q, S0_q, ~In);  // AND_Gate
  and and_8 (and_8_out, ~S2_q, S1_q, S0_q, In);  // AND_Gate
  and and_9 (and_9_out, S2_q, ~S1_q, ~S0_q, ~In);  // AND_Gate
  // AND_Gate and_10 has open pins: in0=S2_q, in1=S1_q, in2=S0_q, in3=In, out=open
  and and_11 (and_11_out, S2_q, ~S1_q, S0_q, ~In);  // AND_Gate
  and and_12 (and_12_out, S2_q, ~S1_q, S0_q, In);  // AND_Gate
  and and_13 (and_4_out, S2_q, S1_q, ~S0_q, ~In);  // AND_Gate
  and and_14 (and_14_out, S2_q, S1_q, ~S0_q, In);  // AND_Gate
  or or_1 (S2, and_1_out, and_4_out, and_3_out, and_7_out, and_8_out, and_11_out);
  or or_2 (S1, and_8_out, and_9_out, and_12_out);
  or or_3 (S0, and_3_out, and_4_out, and_5_out, and_11_out, and_12_out);
  or or_4 (Out, and_4_out, and_14_out);

  // Notes on the sheet:
  //   PROBLEM 3: IMPLEMENTING A STATE MACHINE
  //   INPUT SECTION: Do not change anything here!
  //   You may only change the values of the inputs for testing using the hand tool.
  //   Do not introduce any other input or output pins in the circuit.
  //   To your logic
  //   OUTPUT SECTION: Do not change anything here!
  //   Do not introduce any other input or output pins in the circuit.
  //   From your logic
endmodule
