// Logisim project recitationQ4.circ as structural Verilog: 4 circuits, main circuit main
module main (
  input  A,
  input  B,
  input  C,
  output X
);

  wire and_1_out, and_2_out, and_3_out, and_4_out, and_5_out, and_6_out;

  and and_1 (and_1_out, ~A, ~B, ~C);  // AND_Gate
  and and_2 (and_2_out, ~A, ~B, C);  // AND_Gate
  and and_3 (and_3_out, ~A, B, ~C);  // AND_Gate
  and and_4 (and_4_out, A, ~B, ~C);  // AND_Gate
  and and_5 (and_5_out, A, B, ~C);  // AND_Gate
  and and_6 (and_6_out, A, B, C);
  or or_1 (X, and_1_out, and_2_out, and_3_out, and_4_out, and_5_out, and_6_out);
endmodule

module Q2 (
  input  in_1,
  input  in_2,
  input  in_3,
  output out_4,
  output out_5
);

  wire and_1_out, or_1_out, xor_1_out;

  Transistor #(.\type ("n")) transistor_1 ();  // open: in, out, gate
  and and_1 (and_1_out, in_1, in_2);
  not not_1 (out_5, or_1_out);
  or or_1 (or_1_out, in_2, in_3);
  xor xor_1 (xor_1_out, and_1_out, out_5);
  not not_2 (out_4, xor_1_out);
endmodule

module q14 (
  input  in_1,
  input  in_2,
  input  in_3,
  output out_4,
  output out_5,
  output out_6,
  output out_7,
  output out_8
);

  wire and_1_out, not_1_out, not_3_out, not_5_out, or_2_out;

  not not_1 (not_1_out, in_2);
  or or_1 (out_5, in_1, not_1_out);
  and and_1 (and_1_out, in_2, in_3);
  not not_2 (out_7, and_1_out);
  or or_2 (or_2_out, out_5, out_7);
  not not_3 (not_3_out, out_5);
  not not_4 (out_6, or_2_out);
  not not_5 (not_5_out, out_6);
  and and_2 (out_4, not_3_out, out_6);
  or or_3 (out_8, not_5_out, out_7);
endmodule

module NAND (
  input  in_1,
  input  in_2,
  input  in_3,
  output out_4
);

  nand nand_1 (out_4, in_1, in_2, in_3);
endmodule
